// Logisim project pipelinedCPU16Bit.circ as structural Verilog: 28 circuits, main circuit RegFile
module RegFile (
  input  [2:0] RAOpcode,
  input  [2:0] RBOpcode,
  input  [2:0] RWOpcode,
  input  RegWrite,
  input  [15:0] BusW,
  output [15:0] BusA,
  output [15:0] BusB
);

  wire clk_out, decoder_1_out0, decoder_1_out1, decoder_1_out2, decoder_1_out3, decoder_1_out4,
       decoder_1_out5, decoder_1_out6, decoder_1_out7, decoder_2_out0, decoder_2_out1, decoder_2_out2,
       decoder_2_out3, decoder_2_out4, decoder_2_out5, decoder_2_out6, decoder_2_out7, decoder_3_out0,
       decoder_3_out1, decoder_3_out2, decoder_3_out3, decoder_3_out4, decoder_3_out5, decoder_3_out6,
       decoder_3_out7, regxdecoder_1_p6, regxdecoder_2_p6, regxdecoder_3_p5, regxdecoder_4_p6,
       regxdecoder_5_p5, regxdecoder_6_p5, regxdecoder_7_p3;
  wire [15:0] bit_extender_1_out, bit_extender_2_out, register_1_q, register_2_q, register_3_q, register_4_q,
       register_5_q, register_6_q, register_7_q;

  Decoder #(.enable("false"), .select(3)) decoder_1 (
    .out0(decoder_1_out0), .out1(decoder_1_out1), .out2(decoder_1_out2), .out3(decoder_1_out3),
    .out4(decoder_1_out4), .out5(decoder_1_out5), .out6(decoder_1_out6), .out7(decoder_1_out7), .sel(RWOpcode));
  Clock clk (.out(clk_out));
  Register #(.width(16)) register_1 (.D(BusW), .en(regxdecoder_1_p6), .Q(register_1_q), .clk(clk_out), .clr(1'b0));
  // RegXDecoder regxdecoder_1: pin names not known; wires that end beside it: decoder_1_out0, decoder_1_out1, RegWrite, decoder_1_out2, RegWrite, regxdecoder_1_p6
  Register #(.width(16)) register_2 (.D(BusW), .en(regxdecoder_2_p6), .Q(register_2_q), .clk(clk_out), .clr(1'b0));
  // RegXDecoder regxdecoder_2: pin names not known; wires that end beside it: RWOpcode, decoder_1_out2, RegWrite, decoder_1_out3, RegWrite, regxdecoder_2_p6
  Register #(.width(16)) register_3 (.D(BusW), .en(regxdecoder_3_p5), .Q(register_3_q), .clk(clk_out), .clr(1'b0));
  // RegXDecoder regxdecoder_3: pin names not known; wires that end beside it: RWOpcode, decoder_1_out3, RegWrite, decoder_1_out4, regxdecoder_3_p5
  Register #(.width(16)) register_4 (.D(BusW), .en(regxdecoder_4_p6), .Q(register_4_q), .clk(clk_out), .clr(1'b0));
  // RegXDecoder regxdecoder_4: pin names not known; wires that end beside it: RegWrite, decoder_1_out4, RegWrite, decoder_1_out5, RegWrite, regxdecoder_4_p6
  Register #(.width(16)) register_5 (.D(BusW), .en(regxdecoder_5_p5), .Q(register_5_q), .clk(clk_out), .clr(1'b0));
  // RegXDecoder regxdecoder_5: pin names not known; wires that end beside it: decoder_1_out5, RegWrite, decoder_1_out6, RegWrite, regxdecoder_5_p5
  Register #(.width(16)) register_6 (.D(BusW), .en(regxdecoder_6_p5), .Q(register_6_q), .clk(clk_out), .clr(1'b0));
  // RegXDecoder regxdecoder_6: pin names not known; wires that end beside it: decoder_1_out6, RegWrite, decoder_1_out7, RegWrite, regxdecoder_6_p5
  Register #(.width(16)) register_7 (.D(BusW), .en(regxdecoder_7_p3), .Q(register_7_q), .clk(clk_out), .clr(1'b0));
  // RegXDecoder regxdecoder_7: pin names not known; wires that end beside it: decoder_1_out7, RegWrite, regxdecoder_7_p3
  assign BusA = decoder_2_out4 ? register_4_q : 16'bz;  // Controlled_Buffer controlled_buffer_1
  assign BusA = decoder_2_out5 ? register_5_q : 16'bz;  // Controlled_Buffer controlled_buffer_2
  assign BusA = decoder_2_out6 ? register_6_q : 16'bz;  // Controlled_Buffer controlled_buffer_3
  assign BusA = decoder_2_out7 ? register_7_q : 16'bz;  // Controlled_Buffer controlled_buffer_4
  Decoder #(.enable("false"), .select(3)) decoder_2 (
    .out0(decoder_2_out0), .out1(decoder_2_out1), .out2(decoder_2_out2), .out3(decoder_2_out3),
    .out4(decoder_2_out4), .out5(decoder_2_out5), .out6(decoder_2_out6), .out7(decoder_2_out7), .sel(RAOpcode));
  assign BusA = decoder_2_out1 ? register_1_q : 16'bz;  // Controlled_Buffer controlled_buffer_5
  assign BusA = decoder_2_out2 ? register_2_q : 16'bz;  // Controlled_Buffer controlled_buffer_6
  assign BusA = decoder_2_out3 ? register_3_q : 16'bz;  // Controlled_Buffer controlled_buffer_7
  assign bit_extender_1_out = {{15{1'b0}}, 1'b0};  // Bit_Extender bit_extender_1
  assign BusA = decoder_2_out0 ? bit_extender_1_out : 16'bz;  // Controlled_Buffer controlled_buffer_8
  Decoder #(.enable("false"), .select(3)) decoder_3 (
    .out0(decoder_3_out0), .out1(decoder_3_out1), .out2(decoder_3_out2), .out3(decoder_3_out3),
    .out4(decoder_3_out4), .out5(decoder_3_out5), .out6(decoder_3_out6), .out7(decoder_3_out7), .sel(RBOpcode));
  assign BusB = decoder_3_out4 ? register_4_q : 16'bz;  // Controlled_Buffer controlled_buffer_9
  assign BusB = decoder_3_out5 ? register_5_q : 16'bz;  // Controlled_Buffer controlled_buffer_10
  assign BusB = decoder_3_out6 ? register_6_q : 16'bz;  // Controlled_Buffer controlled_buffer_11
  assign BusB = decoder_3_out7 ? register_7_q : 16'bz;  // Controlled_Buffer controlled_buffer_12
  assign BusB = decoder_3_out1 ? register_1_q : 16'bz;  // Controlled_Buffer controlled_buffer_13
  assign BusB = decoder_3_out2 ? register_2_q : 16'bz;  // Controlled_Buffer controlled_buffer_14
  assign BusB = decoder_3_out3 ? register_3_q : 16'bz;  // Controlled_Buffer controlled_buffer_15
  assign bit_extender_2_out = {{15{1'b0}}, 1'b0};  // Bit_Extender bit_extender_2
  assign BusB = decoder_3_out0 ? bit_extender_2_out : 16'bz;  // Controlled_Buffer controlled_buffer_16
endmodule

// DistFinal
module myCPU (
  input  clear
);

  wire ALUSrc, clock_1_out, EXTOp, kill1, kill2, LUI, MemRd2, MemWr, not_1_out, or_1_out,
       pipelinedctrl_1_alusrc, pipelinedctrl_1_isbeq, pipelinedctrl_1_isbne, pipelinedctrl_1_ishump,
       pipelinedctrl_1_isjr, pipelinedctrl_1_memrd, pipelinedctrl_1_memwr, pipelinedctrl_1_regwr,
       pipelinedctrlex_1_isbeqout, pipelinedctrlex_1_isbneout, pipelinedctrlex_1_memwrout, regdist_1_portb,
       regdist_1_portw, RegWr, RegWr2, RegWr3, stall, zeroFlag;
  wire [1:0] A, B, InstF_q_3, PCOpcode, pipelinedctrl_1_wb, pipelinedctrlex_1_wbout, regDst, RtR7R1, WB;
  wire [2:0] InstF_q, InstF_q_2, multiplexer_3_out, multiplexer_5_out, Rd2, Rd3, RsOpco, RtOpco, Rw;
  wire [4:0] ALUOp, InstF_q_4, Opcode2_q, pipelinedctrl_1_aluopcode;
  wire [15:0] alu_1_out_5, aluRes_q, bit_extender_1_out, branchcirc_1_branchdisrt, btaid_q, ex, ext_1_imm16,
       imm_q, insrtcMem_data, jumpcirc_1_out_2, luiex_q, luiid_q, memRes, mm, multiplexer_1_out,
       multiplexer_2_out, multiplexer_6_out, multiplexer_7_out, multiplexer_8_out, pc_q, pcex_q,
       pcincrementor_1_out_2, PCReg_q, ram_1_dout, regfile_1_busa, regfile_1_busb, Rs_q, Rt2_q, Rt_q,
       shifter_1_out;

  // RegXDecoder regxdecoder_1: pin names not known
  not not_1 (not_1_out, stall);
  Multiplexer #(.select(2), .width(16)) multiplexer_1 (
    .in0(pcincrementor_1_out_2), .in1(btaid_q), .in2(jumpcirc_1_out_2), .in3(multiplexer_6_out),
    .out(multiplexer_1_out));  // open: sel
  PCincrementor pcincrementor_1 (.out_2(pcincrementor_1_out_2));  // open: in_1
  Register #(.width(16)) PCReg (.D(multiplexer_1_out), .en(not_1_out), .Q(PCReg_q), .clk(clock_1_out), .clr(clear));
  Clock clock_1 (.out(clock_1_out));
  ROM #(.addrWidth(16), .dataWidth(16)) insrtcMem (.addr(PCReg_q), .data(insrtcMem_data));
  pipelinedPC pipelinedpc_1 (
    .isBEQ(pipelinedctrlex_1_isbeqout), .isBNE(pipelinedctrlex_1_isbneout), .isJump(pipelinedctrl_1_ishump),
    .isJr(pipelinedctrl_1_isjr), .zero(zeroFlag), .PCOp(PCOpcode), .kill1(kill1), .kill2(kill2));
  branchCirc branchcirc_1 (.displacement({InstF_q_3, InstF_q_2}), .PC(PCReg_q), .branchDisrt(branchcirc_1_branchdisrt));
  jumpCirc jumpcirc_1 (.imm11({InstF_q_3, InstF_q_2, RsOpco, InstF_q}), .out_2(jumpcirc_1_out_2));
  Multiplexer #(.width(16)) multiplexer_2 (
    .in0(insrtcMem_data), .in1({16{1'b0}}), .out(multiplexer_2_out), .sel(kill1));
  Register #(.width(16)) InstF (
    .D(multiplexer_2_out), .en(not_1_out), .Q({InstF_q_4, InstF_q_3, InstF_q_2, RsOpco, InstF_q}),
    .clk(clock_1_out));  // open: clr
  RegDist regdist_1 (.regDst(regDst), .PortW(regdist_1_portw), .PortB(regdist_1_portb));
  Multiplexer #(.select(2), .width(3)) multiplexer_3 (
    .in0(InstF_q), .in1(3'b111), .in2(3'b001), .out(multiplexer_3_out), .sel(RtR7R1));  // open: in3
  dataHazDet datahazdet_1 (
    .RsOpcode(RsOpco), .RtOpcode(RtOpco), .Rd2(Rd2), .Rd3(Rd3), .Rd4(Rw), .MemRd2(MemRd2), .RegWrite4(RegWr),
    .RegWrite2(RegWr2), .RegWrite3(RegWr3), .stall(stall), .frwrdA(A), .frwrdB(B));
  Multiplexer #(.width(3)) multiplexer_4 (
    .in0(multiplexer_3_out), .in1(InstF_q_2), .out(RtOpco), .sel(regdist_1_portb));
  ext ext_1 (.imm5({InstF_q_3, InstF_q_2}), .extOp(EXTOp), .imm16(ext_1_imm16));
  Multiplexer #(.width(3)) multiplexer_5 (
    .in0(multiplexer_3_out), .in1(InstF_q_2), .out(multiplexer_5_out), .sel(regdist_1_portw));
  assign bit_extender_1_out = {{5{1'b0}}, {InstF_q_3, InstF_q_2, RsOpco, InstF_q}};  // Bit_Extender bit_extender_1
  pipelinedCtrl pipelinedctrl_1 (
    .Opcode(InstF_q_4), .Funct(InstF_q_3), .ALUOpcode(pipelinedctrl_1_aluopcode), .EXTOp(EXTOp),
    .RegWR(pipelinedctrl_1_regwr), .MEMRd(pipelinedctrl_1_memrd), .MEMWr(pipelinedctrl_1_memwr),
    .ALUSrc(pipelinedctrl_1_alusrc), .RtR7R1(RtR7R1), .WB(pipelinedctrl_1_wb), .RegDst(regDst),
    .isBEQ(pipelinedctrl_1_isbeq), .isBNE(pipelinedctrl_1_isbne), .isHump(pipelinedctrl_1_ishump),
    .isJR(pipelinedctrl_1_isjr));
  Shifter #(.width(16)) shifter_1 (.in(bit_extender_1_out), .\dist (4'b0101), .out(shifter_1_out));
  RegFile regfile_1 (
    .RegWrite(RegWr), .BusW(memRes), .RWOpcode(Rw), .RAOpcode(RsOpco), .RBOpcode(RtOpco),
    .BusB(regfile_1_busb), .BusA(regfile_1_busa));
  Multiplexer #(.select(2), .width(16)) multiplexer_6 (
    .in0(regfile_1_busa), .in1(ex), .in2(mm), .in3(memRes), .out(multiplexer_6_out));  // open: sel
  Multiplexer #(.select(2), .width(16)) multiplexer_7 (
    .in0(regfile_1_busb), .in1(ex), .in2(mm), .in3(memRes), .out(multiplexer_7_out), .sel(B));
  or or_1 (or_1_out, stall, kill2);
  Register #(.width(16)) pc (.D(PCReg_q), .Q(pc_q), .clk(clock_1_out));  // open: en, clr
  Register #(.width(16)) btaid (.D(branchcirc_1_branchdisrt), .Q(btaid_q), .clk(clock_1_out));  // open: en, clr
  Register #(.width(16)) luiid (.D(shifter_1_out), .Q(luiid_q), .clk(clock_1_out));  // open: en, clr
  Register #(.width(16)) Rs (.D(multiplexer_6_out), .Q(Rs_q), .clk(clock_1_out));  // open: en, clr
  Register #(.width(16)) Rt (.D(multiplexer_7_out), .Q(Rt_q), .clk(clock_1_out));  // open: en, clr
  Register #(.width(16)) imm (.D(ext_1_imm16), .Q(imm_q), .clk(clock_1_out));  // open: en, clr
  Register #(.width(3)) u_Rd2 (.D(multiplexer_5_out), .Q(Rd2), .clk(clock_1_out));  // open: en, clr
  pipelinedCtrlEX pipelinedctrlex_1 (
    .WB(pipelinedctrl_1_wb), .RegWr(pipelinedctrl_1_regwr), .ALUSrc(pipelinedctrl_1_alusrc),
    .ALUOp(pipelinedctrl_1_aluopcode), .isBEQ(pipelinedctrl_1_isbeq), .isBNE(pipelinedctrl_1_isbne),
    .MemWr(pipelinedctrl_1_memwr), .clr(or_1_out), .WBOut(pipelinedctrlex_1_wbout), .RegWrOut(RegWr2),
    .ALUSrcOut(ALUSrc), .ALUOpOut(ALUOp), .isBEQOut(pipelinedctrlex_1_isbeqout),
    .isBNEOut(pipelinedctrlex_1_isbneout), .MemWrOut(pipelinedctrlex_1_memwrout));
  Register #(.width(1)) u_MemRd2 (.D(pipelinedctrl_1_memrd), .Q(MemRd2), .clk(clock_1_out));  // open: en, clr
  Register #(.width(5)) Opcode2 (.D(InstF_q_4), .Q(Opcode2_q), .clk(clock_1_out));  // open: en, clr
  Multiplexer #(.width(16)) multiplexer_8 (.in0(Rt_q), .in1(imm_q), .out(multiplexer_8_out), .sel(ALUSrc));
  isLUI islui_1 (.Opcode2(Opcode2_q), .isLUI(LUI));
  Multiplexer #(.width(16)) multiplexer_9 (.in0(alu_1_out_5), .in1(luiid_q), .out(ex), .sel(LUI));
  ALU alu_1 (
    .data1(Rs_q), .data2(multiplexer_8_out), .ALUOp(ALUOp), .out_5(alu_1_out_5), .zeroFlag(zeroFlag));  // open: overflow
  Register #(.width(16)) pcex (.D(pc_q), .Q(pcex_q), .clk(clock_1_out));  // open: en, clr
  Register #(.width(16)) luiex (.D(luiid_q), .Q(luiex_q), .clk(clock_1_out));  // open: en, clr
  Register #(.width(16)) aluRes (.D(ex), .Q(aluRes_q), .clk(clock_1_out));  // open: en, clr
  Register #(.width(16)) Rt2 (.D(Rt_q), .Q(Rt2_q), .clk(clock_1_out));  // open: en, clr
  Register #(.width(3)) u_Rd3 (.D(Rd2), .Q(Rd3), .clk(clock_1_out));  // open: en, clr
  pipelinedCtrMEM pipelinedctrmem_1 (
    .WB(pipelinedctrlex_1_wbout), .RegWr(RegWr2), .MemWr(pipelinedctrlex_1_memwrout), .WBOut(WB),
    .RegWrOut(RegWr3), .MemWrOut(MemWr));
  RAM #(.addrWidth(16), .dataWidth(16), .enables("line")) ram_1 (
    .addr(aluRes_q), .we(MemWr), .clk(clock_1_out), .din(Rt2_q), .dout(ram_1_dout));
  Multiplexer #(.select(2), .width(16)) multiplexer_10 (
    .in0(aluRes_q), .in1(ram_1_dout), .in2(pcex_q), .in3(luiex_q), .out(mm), .sel(WB));
  Register #(.width(16)) u_memRes (.D(mm), .Q(memRes), .clk(clock_1_out));  // open: en, clr
  Register #(.width(3)) Rd4 (.D(Rd3), .Q(Rw), .clk(clock_1_out));  // open: en, clr
  Register #(.width(1)) u_RegWr (.D(RegWr3), .Q(RegWr), .clk(clock_1_out));  // open: en, clr

  // Other names for the same wires on the sheet: wb_t[15:0] = memRes

  // Notes on the sheet:
  //   contents of insrtcMem (hex, n*v repeats v):
  //   4283 4004 40c5 6815 4064 4052 7f63 4001 883a 8024 0 c92 4243 4006 680e 4049 4076 680e 67cc 600d 1ac
  //   4049 4052 7e93 1e38 34*0 c92 4243 4006 680e 4049 4076 680e 67cc 600d 1ac 4049 4052 7e53 1e38
endmodule

module ALU (
  input  [15:0] data1,
  input  [15:0] data2,
  input  [4:0] ALUOp,
  output overflow,
  output [15:0] out_5,
  output zeroFlag
);

  wire [15:0] addsub_1_result, and_1_out, barrelshifter_1_out_4, multiplexer_1_out, mycomparator_1_out_4,
       nor_1_out, or_1_out, reverser_1_out_4, xor_1_out;

  myComparator mycomparator_1 (.in_3(ALUOp[3]), .in_1(data1), .in_2(data2), .out_4(mycomparator_1_out_4));
  addsub addsub_1 (.data1(data1), .data2(data2), .SelecLine(ALUOp[3]), .result(addsub_1_result), .overflow(overflow));
  assign and_1_out = data1 & data2;  // AND_Gate and_1, 16 bits wide
  assign or_1_out = data1 | data2;  // OR_Gate or_1, 16 bits wide
  assign xor_1_out = data1 ^ data2;  // XOR_Gate xor_1, 16 bits wide
  assign nor_1_out = ~(data1 | data2);  // NOR_Gate nor_1, 16 bits wide
  barrelShifter barrelshifter_1 (.in_3(ALUOp[4:3]), .in_1(data1), .in_2(data2), .out_4(barrelshifter_1_out_4));
  reverser reverser_1 (.in_2(ALUOp[4:3]), .Rd(data2), .Rs(data1), .out_4(reverser_1_out_4));
  Multiplexer #(.select(2), .width(16)) multiplexer_1 (
    .in0(and_1_out), .in1(or_1_out), .in2(xor_1_out), .in3(nor_1_out), .out(multiplexer_1_out),
    .sel(ALUOp[4:3]));
  Multiplexer #(.select(3), .width(16)) multiplexer_2 (
    .in0(addsub_1_result), .in1(mycomparator_1_out_4), .in2(multiplexer_1_out), .in3(barrelshifter_1_out_4),
    .in4(reverser_1_out_4), .in5({16{1'b0}}), .in6({16{1'b0}}), .in7({16{1'b0}}), .out(out_5),
    .sel(ALUOp[2:0]));
  izZero izzero_1 (.in_1(out_5), .out_2(zeroFlag));
endmodule

module SLTSigned (
  input  [15:0] in_1,
  input  [15:0] in_2,
  output [15:0] out_3
);

  wire comparator_1_lt;

  Comparator #(.width(16)) comparator_1 (.a(in_1), .b(in_2), .lt(comparator_1_lt));  // open: gt, eq
  assign out_3 = {{15{1'b0}}, comparator_1_lt};  // Bit_Extender bit_extender_1
endmodule

module SLTUn (
  input  [15:0] in_1,
  input  [15:0] in_2,
  output [15:0] out_3
);

  wire comparator_1_lt;

  Comparator #(.mode("unsigned"), .width(16)) comparator_1 (.a(in_1), .b(in_2), .lt(comparator_1_lt));  // open: gt, eq
  assign out_3 = {{15{1'b0}}, comparator_1_lt};  // Bit_Extender bit_extender_1
endmodule

module barrelShifter (
  input  [15:0] in_1,
  input  [15:0] in_2,
  input  [1:0] in_3,
  output [15:0] out_4
);

  wire [15:0] shifter_1_out, shifter_2_out, shifter_3_out, shifter_4_out;

  Shifter #(.width(16)) shifter_1 (.in(in_1), .\dist (in_2[3:0]), .out(shifter_1_out));
  Shifter #(.shift("lr"), .width(16)) shifter_2 (.in(in_1), .\dist (in_2[3:0]), .out(shifter_2_out));
  Shifter #(.shift("ar"), .width(16)) shifter_3 (.in(in_1), .\dist (in_2[3:0]), .out(shifter_3_out));
  Shifter #(.shift("rr"), .width(16)) shifter_4 (.in(in_1), .\dist (in_2[3:0]), .out(shifter_4_out));
  Multiplexer #(.select(2), .width(16)) multiplexer_1 (
    .in0(shifter_1_out), .in1(shifter_2_out), .in2(shifter_3_out), .in3(shifter_4_out), .out(out_4),
    .sel(in_3));
endmodule

module myComparator (
  input  [15:0] in_1,
  input  [15:0] in_2,
  input  in_3,
  output [15:0] out_4
);

  wire [15:0] sltsigned_1_out_3, sltun_1_out_3;

  SLTSigned sltsigned_1 (.in_2(in_2), .in_1(in_1), .out_3(sltsigned_1_out_3));
  SLTUn sltun_1 (.in_2(in_2), .in_1(in_1), .out_3(sltun_1_out_3));
  Multiplexer #(.width(16)) multiplexer_1 (.in0(sltsigned_1_out_3), .in1(sltun_1_out_3), .out(out_4), .sel(in_3));
endmodule

module reverser (
  input  [15:0] Rs,
  input  [1:0] in_2,
  input  [15:0] Rd,
  output [15:0] out_4
);

  Multiplexer #(.select(2), .width(16)) multiplexer_1 (
    .in0({Rd[15:8], Rs[0], Rs[1], Rs[2], Rs[3], Rs[4], Rs[5], Rs[6], Rs[7]}),
    .in1({Rd[15:8], Rs[8], Rs[9], Rs[10], Rs[11], Rs[12], Rs[13], Rs[14], Rs[15]}),
    .in2({Rs[0], Rs[1], Rs[2], Rs[3], Rs[4], Rs[5], Rs[6], Rs[7], Rs[8], Rs[9], Rs[10], Rs[11], Rs[12], Rs[13], Rs[14], Rs[15]}),
    .in3({16{1'b0}}), .out(out_4), .sel(in_2));
endmodule

module izZero (
  input  [15:0] in_1,
  output out_2
);

  wire [15:0] sltun_1_out_3;
  wire [15:1] xor_1_out;

  SLTUn sltun_1 (.in_2(in_1), .in_1({16{1'b0}}), .out_3(sltun_1_out_3));
  assign {xor_1_out, out_2} = sltun_1_out_3 ^ 16'h1;  // XOR_Gate xor_1, 16 bits wide
endmodule

module RegDist (
  input  [1:0] regDst,
  output PortB,
  output PortW
);

  not not_1 (PortW, regDst[1]);

  assign PortB = regDst[0];
endmodule

module ext (
  input  [4:0] imm5,
  input  extOp,
  output [15:0] imm16
);

  wire [15:0] bit_extender_1_out, bit_extender_2_out;

  assign bit_extender_1_out = {{11{1'b0}}, imm5};  // Bit_Extender bit_extender_1
  assign bit_extender_2_out = {{11{imm5[4]}}, imm5};  // Bit_Extender bit_extender_2
  Multiplexer #(.width(16)) multiplexer_1 (
    .in0(bit_extender_1_out), .in1(bit_extender_2_out), .out(imm16), .sel(extOp));
endmodule

module jumpCirc (
  input  [10:0] imm11,
  output [15:0] out_2
);

  assign out_2 = {{5{1'b0}}, imm11};  // Bit_Extender bit_extender_1
endmodule

module branchCirc (
  input  [4:0] displacement,
  input  [15:0] PC,
  output [15:0] branchDisrt
);

  wire [15:0] ext_1_imm16;

  ext ext_1 (.imm5(displacement), .extOp(1'b1), .imm16(ext_1_imm16));
  Adder #(.width(16)) adder_1 (.a(ext_1_imm16), .b(PC), .out(branchDisrt));  // open: cin, cout
endmodule

module mainCtrl (
  input  [4:0] OPcode,
  output [1:0] RtR7R1,
  output [1:0] RegDst,
  output ALUSrc,
  output EXTOp,
  output RegWR,
  output [1:0] WB,
  output MEMRd,
  output MEMWr
);

  wire decoder_1_out0, decoder_1_out1, decoder_1_out2, decoder_1_out8, decoder_1_out9, decoder_1_out10,
       decoder_1_out11, decoder_1_out14, decoder_1_out15, decoder_1_out16;

  Decoder #(.enable("false"), .select(5)) decoder_1 (
    .out0(decoder_1_out0), .out1(decoder_1_out1), .out2(decoder_1_out2), .out3(RegDst[0]),
    .out8(decoder_1_out8), .out9(decoder_1_out9), .out10(decoder_1_out10), .out11(decoder_1_out11),
    .out12(MEMRd), .out13(MEMWr), .out14(decoder_1_out14), .out15(decoder_1_out15), .out16(decoder_1_out16),
    .out17(RtR7R1[0]), .out31(RtR7R1[1]), .sel(OPcode));  // open: out4, out5, out6, out7, out18, out19, out20, out21, out22, out23, out24, out25, out26, out27, out28, out29, out30
  or or_1 (RegDst[1], decoder_1_out8, decoder_1_out9, decoder_1_out10, decoder_1_out11, MEMRd, RtR7R1[0], RtR7R1[1]);
  or or_2 (ALUSrc, decoder_1_out8, decoder_1_out9, decoder_1_out10, decoder_1_out11, MEMRd, MEMWr);
  or or_3 (EXTOp, MEMRd, MEMWr, decoder_1_out8, decoder_1_out14, decoder_1_out15);
  nor nor_1 (RegWR, MEMWr, decoder_1_out14, decoder_1_out15, decoder_1_out16);
  or or_4 (WB[1], RtR7R1[0], RtR7R1[1]);
  or or_5 (WB[0], MEMRd, RtR7R1[1]);
endmodule

module ALUCtrl (
  input  [4:0] Opcode,
  input  [1:0] Funct,
  output [4:0] ALUOpcode
);

  wire and_1_out, and_2_out, and_3_out, and_4_out, and_5_out, and_6_out, and_7_out, and_8_out, and_9_out,
       and_10_out, and_11_out, and_12_out, and_13_out, and_14_out, and_15_out, and_16_out, not_1_out,
       not_2_out, not_3_out, not_4_out, not_5_out, not_6_out, not_7_out;

  not not_1 (not_1_out, Opcode[4]);
  not not_2 (not_2_out, Opcode[3]);
  not not_3 (not_3_out, Opcode[2]);
  not not_4 (not_4_out, Opcode[1]);
  not not_5 (not_5_out, Opcode[0]);
  not not_6 (not_6_out, Funct[1]);
  not not_7 (not_7_out, Funct[0]);
  and and_1 (and_1_out, not_1_out, not_2_out, not_4_out, Opcode[0], Funct[1]);
  and and_2 (and_2_out, not_2_out, Opcode[1], not_5_out, Funct[1]);
  and and_3 (and_3_out, Opcode[3], not_3_out, Opcode[1], Opcode[0]);
  and and_4 (and_4_out, not_2_out, Opcode[1], Funct[1], not_7_out);
  and and_5 (and_5_out, not_1_out, not_2_out, not_4_out, Funct[0]);
  and and_6 (and_6_out, Opcode[3], Opcode[1], not_5_out);
  and and_7 (and_7_out, not_1_out, Opcode[2], Opcode[1]);
  and and_8 (and_8_out, Opcode[1], not_5_out, Funct[0]);
  and and_9 (and_9_out, not_1_out, not_2_out, not_6_out, Funct[0]);
  and and_10 (and_10_out, not_2_out, Opcode[1], Opcode[0], not_6_out);
  and and_11 (and_11_out, not_2_out, Opcode[1], Opcode[0], not_7_out);
  and and_12 (and_12_out, not_1_out, not_3_out, not_4_out, Opcode[0]);
  and and_13 (and_13_out, not_3_out, Opcode[1], not_5_out);
  and and_14 (and_14_out, Opcode[3], not_3_out, Opcode[0]);
  and and_15 (and_15_out, not_1_out, not_2_out, not_5_out, Funct[1]);
  and and_16 (and_16_out, not_2_out, Opcode[1], not_5_out);
  or or_1 (ALUOpcode[4], and_1_out, and_2_out, and_3_out, and_4_out);
  or or_2 (ALUOpcode[3], and_5_out, and_6_out, and_7_out, and_8_out, and_9_out);
  or or_3 (ALUOpcode[2], and_10_out, and_11_out);
  or or_4 (ALUOpcode[1], and_12_out, and_13_out, and_14_out);
  or or_5 (ALUOpcode[0], and_15_out, and_16_out);
endmodule

module addsub (
  input  [15:0] data1,
  input  [15:0] data2,
  input  SelecLine,
  output [15:0] result,
  output overflow
);

  wire adder_1_cout, subtractor_1_bout;
  wire [15:0] adder_1_out, subtractor_1_out;

  Adder #(.width(16)) adder_1 (.a(data1), .b(data2), .out(adder_1_out), .cout(adder_1_cout));  // open: cin
  Subtractor #(.width(16)) subtractor_1 (
    .a(data1), .b(data2), .out(subtractor_1_out), .bout(subtractor_1_bout));  // open: bin
  Multiplexer #(.width(16)) multiplexer_1 (.in0(adder_1_out), .in1(subtractor_1_out), .out(result), .sel(SelecLine));
  Multiplexer multiplexer_2 (.in0(adder_1_cout), .in1(subtractor_1_bout), .out(overflow), .sel(SelecLine));
endmodule

module PCCtrl (
  input  zero,
  input  [1:0] funct,
  input  [4:0] Opcode,
  output [1:0] PCSrc
);

  wire and_1_out, and_2_out, and_3_out, and_4_out, decoder_1_out3, decoder_1_out14, decoder_1_out15,
       decoder_1_out16, decoder_1_out17, decoder_2_out0, decoder_2_out1, decoder_3_out3;

  Decoder #(.enable("false"), .select(5)) decoder_1 (
    .out3(decoder_1_out3), .out14(decoder_1_out14), .out15(decoder_1_out15), .out16(decoder_1_out16),
    .out17(decoder_1_out17), .sel(Opcode));  // open: out0, out1, out2, out4, out5, out6, out7, out8, out9, out10, out11, out12, out13, out18, out19, out20, out21, out22, out23, out24, out25, out26, out27, out28, out29, out30, out31
  Decoder #(.enable("false")) decoder_2 (.out0(decoder_2_out0), .out1(decoder_2_out1), .sel(zero));
  Decoder #(.enable("false"), .select(2)) decoder_3 (.out3(decoder_3_out3), .sel(funct));  // open: out0, out1, out2
  and and_1 (and_1_out, decoder_1_out3, decoder_3_out3);
  and and_2 (and_2_out, decoder_1_out3, decoder_3_out3);
  and and_3 (and_3_out, decoder_1_out14, decoder_2_out1);
  and and_4 (and_4_out, decoder_1_out15, decoder_2_out0);
  or or_1 (PCSrc[1], and_1_out, decoder_1_out16, decoder_1_out17);
  or or_2 (PCSrc[0], and_2_out, and_3_out, and_4_out);
endmodule

module SCCPU (
  input  clear,
  output out_2
);

  wire alu_1_zeroflag, clock_1_out, mainctrl_1_alusrc, mainctrl_1_extop, mainctrl_1_memrd, mainctrl_1_memwr,
       mainctrl_1_regwr, regdist_1_portb, regdist_1_portw;
  wire [1:0] insrtcMem_data_3, mainctrl_1_regdst, mainctrl_1_rtr7r1, mainctrl_1_wb, pcctrl_1_pcsrc;
  wire [2:0] insrtcMem_data_2, multiplexer_2_out, multiplexer_3_out, multiplexer_4_out;
  wire [4:0] aluctrl_1_aluopcode, insrtcMem_data_4;
  wire [5:0] insrtcMem_data;
  wire [15:0] alu_1_out_5, bit_extender_1_out, branchcirc_1_branchdisrt, ext_1_imm16, jumpcirc_1_out_2,
       multiplexer_1_out, multiplexer_5_out, multiplexer_6_out, pcincrementor_1_out_2, PCReg_q, ram_1_dout,
       regfile_1_busa, regfile_1_busb, shifter_1_out;

  Multiplexer #(.select(2), .width(16)) multiplexer_1 (
    .in0(pcincrementor_1_out_2), .in1(branchcirc_1_branchdisrt), .in2(jumpcirc_1_out_2), .in3(alu_1_out_5),
    .out(multiplexer_1_out));  // open: sel
  Clock clock_1 (.out(clock_1_out));
  PCincrementor pcincrementor_1 (.out_2(pcincrementor_1_out_2));  // open: in_1
  Register #(.width(16)) PCReg (.D(multiplexer_1_out), .en(clock_1_out), .Q(PCReg_q), .clk(clock_1_out), .clr(clear));
  ROM #(.addrWidth(16), .dataWidth(16)) insrtcMem (
    .addr(PCReg_q), .data({insrtcMem_data_4, insrtcMem_data_3, insrtcMem_data_2, insrtcMem_data}));
  jumpCirc jumpcirc_1 (.imm11({insrtcMem_data_3, insrtcMem_data_2, insrtcMem_data}), .out_2(jumpcirc_1_out_2));
  PCCtrl pcctrl_1 (.Opcode(insrtcMem_data_4), .zero(alu_1_zeroflag), .funct(insrtcMem_data_3), .PCSrc(pcctrl_1_pcsrc));
  branchCirc branchcirc_1 (
    .displacement({insrtcMem_data_3, insrtcMem_data_2}), .PC(pcincrementor_1_out_2),
    .branchDisrt(branchcirc_1_branchdisrt));
  RegDist regdist_1 (.regDst(mainctrl_1_regdst), .PortW(regdist_1_portw), .PortB(regdist_1_portb));
  Multiplexer #(.select(2), .width(3)) multiplexer_2 (
    .in0(insrtcMem_data[2:0]), .in1(3'b111), .in2(3'b001), .out(multiplexer_2_out), .sel(mainctrl_1_rtr7r1));  // open: in3
  ext ext_1 (.imm5({insrtcMem_data_3, insrtcMem_data_2}), .extOp(mainctrl_1_extop), .imm16(ext_1_imm16));
  mainCtrl mainctrl_1 (
    .OPcode(insrtcMem_data_4), .EXTOp(mainctrl_1_extop), .RegWR(mainctrl_1_regwr), .MEMRd(mainctrl_1_memrd),
    .MEMWr(mainctrl_1_memwr), .ALUSrc(mainctrl_1_alusrc), .RtR7R1(mainctrl_1_rtr7r1), .WB(mainctrl_1_wb),
    .RegDst(mainctrl_1_regdst));
  Multiplexer #(.width(3)) multiplexer_3 (
    .in0(multiplexer_2_out), .in1(insrtcMem_data_2), .out(multiplexer_3_out), .sel(regdist_1_portb));
  assign bit_extender_1_out = {{5{1'b0}}, {insrtcMem_data_3, insrtcMem_data_2, insrtcMem_data}};  // Bit_Extender bit_extender_1
  Multiplexer #(.width(3)) multiplexer_4 (
    .in0(multiplexer_2_out), .in1(insrtcMem_data_2), .out(multiplexer_4_out), .sel(regdist_1_portw));
  Shifter #(.width(16)) shifter_1 (.in(bit_extender_1_out), .\dist (4'b0101), .out(shifter_1_out));
  RegFile regfile_1 (
    .RegWrite(mainctrl_1_regwr), .BusW(multiplexer_6_out), .RWOpcode(multiplexer_4_out),
    .RAOpcode(insrtcMem_data[5:3]), .RBOpcode(multiplexer_3_out), .BusB(regfile_1_busb), .BusA(regfile_1_busa));
  Multiplexer #(.width(16)) multiplexer_5 (
    .in0(regfile_1_busb), .in1(ext_1_imm16), .out(multiplexer_5_out), .sel(mainctrl_1_alusrc));
  ALUCtrl aluctrl_1 (.Opcode(insrtcMem_data_4), .Funct(insrtcMem_data_3), .ALUOpcode(aluctrl_1_aluopcode));
  ALU alu_1 (
    .data1(regfile_1_busa), .data2(multiplexer_5_out), .ALUOp(aluctrl_1_aluopcode), .out_5(alu_1_out_5),
    .zeroFlag(alu_1_zeroflag));  // open: overflow
  RAM #(.addrWidth(16), .dataWidth(16), .enables("line")) ram_1 (
    .addr(alu_1_out_5), .we(mainctrl_1_memwr), .clk(clock_1_out), .din(regfile_1_busb), .dout(ram_1_dout));
  Multiplexer #(.select(2), .width(16)) multiplexer_6 (
    .in0(alu_1_out_5), .in1(ram_1_dout), .in2(pcincrementor_1_out_2), .in3(shifter_1_out),
    .out(multiplexer_6_out), .sel(mainctrl_1_wb));

  // Notes on the sheet:
  //   contents of insrtcMem (hex, n*v repeats v):
  //   1e18
endmodule

module mainxaluctrl (
  input  [4:0] OPcode,
  input  [1:0] Funct,
  output [1:0] RtR7R1,
  output [1:0] RegDst,
  output BranchType,
  output ALUSrc,
  output JumpType,
  output EXTOp,
  output RegWR,
  output [1:0] WB,
  output MEMRd,
  output MEMWr,
  output [4:0] ALUOpcode,
  output JrType
);

  wire and_1_out, and_2_out, and_3_out, and_4_out, and_5_out, and_6_out, and_7_out, and_8_out, and_9_out,
       and_10_out, and_11_out, and_12_out, and_13_out, and_14_out, and_15_out, and_16_out, decoder_1_out0,
       decoder_1_out1, decoder_1_out2, decoder_1_out8, decoder_1_out9, decoder_1_out10, decoder_1_out11,
       decoder_1_out14, decoder_1_out15, decoder_1_out16, not_1_out, not_2_out, not_3_out, not_4_out,
       not_5_out, not_6_out, not_7_out;

  Decoder #(.enable("false"), .select(5)) decoder_1 (
    .out0(decoder_1_out0), .out1(decoder_1_out1), .out2(decoder_1_out2), .out3(RegDst[0]),
    .out8(decoder_1_out8), .out9(decoder_1_out9), .out10(decoder_1_out10), .out11(decoder_1_out11),
    .out12(MEMRd), .out13(MEMWr), .out14(decoder_1_out14), .out15(decoder_1_out15), .out16(decoder_1_out16),
    .out17(MEMWr), .out31(RtR7R1[1]), .sel(OPcode));  // open: out4, out5, out6, out7, out18, out19, out20, out21, out22, out23, out24, out25, out26, out27, out28, out29, out30
  not not_1 (not_1_out, OPcode[4]);
  not not_2 (not_2_out, OPcode[3]);
  not not_3 (not_3_out, OPcode[2]);
  not not_4 (not_4_out, OPcode[1]);
  not not_5 (not_5_out, OPcode[0]);
  not not_6 (not_6_out, Funct[1]);
  not not_7 (not_7_out, Funct[0]);
  and and_1 (and_1_out, not_1_out, not_2_out, not_4_out, OPcode[0], Funct[1]);
  and and_2 (and_2_out, not_2_out, OPcode[1], not_5_out, Funct[1]);
  and and_3 (and_3_out, OPcode[3], not_3_out, OPcode[1], OPcode[0]);
  and and_4 (and_4_out, not_2_out, OPcode[1], Funct[1], not_7_out);
  and and_5 (and_5_out, not_1_out, not_2_out, not_4_out, Funct[0]);
  and and_6 (and_6_out, OPcode[3], OPcode[1], not_5_out);
  and and_7 (and_7_out, not_1_out, OPcode[2], OPcode[1]);
  and and_8 (and_8_out, OPcode[1], not_5_out, Funct[0]);
  and and_9 (and_9_out, not_1_out, not_2_out, not_6_out, Funct[0]);
  and and_10 (and_10_out, not_2_out, OPcode[1], OPcode[0], not_6_out);
  or or_1 (ALUOpcode[2], and_10_out, and_11_out);
  and and_11 (and_11_out, not_2_out, OPcode[1], OPcode[0], not_7_out);
  and and_12 (and_12_out, not_1_out, not_3_out, not_4_out, OPcode[0]);
  and and_13 (and_13_out, not_3_out, OPcode[1], not_5_out);
  or or_2 (ALUOpcode[1], and_12_out, and_13_out, and_14_out);
  and and_14 (and_14_out, OPcode[3], not_3_out, OPcode[0]);
  and and_15 (and_15_out, not_1_out, not_2_out, not_5_out, Funct[1]);
  or or_3 (ALUOpcode[0], and_15_out, and_16_out);
  and and_16 (and_16_out, not_2_out, OPcode[1], not_5_out);
  or or_4 (ALUOpcode[4], and_1_out, and_2_out, and_3_out, and_4_out);
  or or_5 (ALUOpcode[3], and_5_out, and_6_out, and_7_out, and_8_out, and_9_out);
  or or_6 (RegDst[1], decoder_1_out8, decoder_1_out9, decoder_1_out10, decoder_1_out11, MEMRd, MEMWr, RtR7R1[1]);
  or or_7 (ALUSrc, decoder_1_out8, decoder_1_out9, decoder_1_out10, decoder_1_out11, MEMRd, MEMWr);
  or or_8 (EXTOp, MEMRd, MEMWr, decoder_1_out8, decoder_1_out14, decoder_1_out15);
  nor nor_1 (RegWR, MEMWr, decoder_1_out14, decoder_1_out15, decoder_1_out16);
  or or_9 (WB[1], MEMWr, RtR7R1[1]);
  or or_10 (WB[0], MEMRd, RtR7R1[1]);
  and and_17 (JrType, Funct[0], Funct[1], RegDst[0]);
  or or_11 (BranchType, decoder_1_out15, decoder_1_out14);
  or or_12 (JumpType, decoder_1_out16, MEMWr);

  assign RtR7R1[0] = MEMWr;
endmodule

module PCCtrlPipelined (
  input  isBranch,
  input  isJump,
  input  isJr,
  output PCSrc
);

  and and_1 (PCSrc, isBranch, isJump, isJr);
endmodule

module pipelinedCtrl (
  input  [4:0] Opcode,
  input  [1:0] Funct,
  output [1:0] RtR7R1,
  output [1:0] RegDst,
  output ALUSrc,
  output EXTOp,
  output isBEQ,
  output RegWR,
  output isBNE,
  output isHump,
  output [1:0] WB,
  output MEMRd,
  output MEMWr,
  output [4:0] ALUOpcode,
  output isJR
);

  wire and_1_out, and_2_out, and_3_out, and_4_out, and_5_out, and_6_out, and_7_out, and_8_out, and_9_out,
       and_10_out, and_11_out, and_12_out, and_13_out, and_14_out, and_15_out, and_16_out, decoder_1_out0,
       decoder_1_out1, decoder_1_out2, decoder_1_out8, decoder_1_out9, decoder_1_out10, decoder_1_out11,
       decoder_1_out16, not_1_out, not_2_out, not_3_out, not_4_out, not_5_out, not_6_out, not_7_out;

  Decoder #(.enable("false"), .select(5)) decoder_1 (
    .out0(decoder_1_out0), .out1(decoder_1_out1), .out2(decoder_1_out2), .out3(RegDst[0]),
    .out8(decoder_1_out8), .out9(decoder_1_out9), .out10(decoder_1_out10), .out11(decoder_1_out11),
    .out12(MEMRd), .out13(MEMWr), .out14(isBEQ), .out15(isBNE), .out16(decoder_1_out16), .out17(RtR7R1[0]),
    .out31(RtR7R1[1]), .sel(Opcode));  // open: out4, out5, out6, out7, out18, out19, out20, out21, out22, out23, out24, out25, out26, out27, out28, out29, out30
  not not_1 (not_1_out, Opcode[4]);
  not not_2 (not_2_out, Opcode[3]);
  not not_3 (not_3_out, Opcode[2]);
  not not_4 (not_4_out, Opcode[1]);
  not not_5 (not_5_out, Opcode[0]);
  not not_6 (not_6_out, Funct[1]);
  not not_7 (not_7_out, Funct[0]);
  and and_1 (and_1_out, not_1_out, not_2_out, not_4_out, Opcode[0], Funct[1]);
  and and_2 (and_2_out, not_2_out, Opcode[1], not_5_out, Funct[1]);
  and and_3 (and_3_out, Opcode[3], not_3_out, Opcode[1], Opcode[0]);
  and and_4 (and_4_out, not_2_out, Opcode[1], Funct[1], not_7_out);
  and and_5 (and_5_out, not_1_out, not_2_out, not_4_out, Funct[0]);
  and and_6 (and_6_out, Opcode[3], Opcode[1], not_5_out);
  and and_7 (and_7_out, not_1_out, Opcode[2], Opcode[1]);
  and and_8 (and_8_out, Opcode[1], not_5_out, Funct[0]);
  and and_9 (and_9_out, not_1_out, not_2_out, not_6_out, Funct[0]);
  and and_10 (and_10_out, not_2_out, Opcode[1], Opcode[0], not_6_out);
  and and_11 (and_11_out, not_2_out, Opcode[1], Opcode[0], not_7_out);
  and and_12 (and_12_out, not_1_out, not_3_out, not_4_out, Opcode[0]);
  and and_13 (and_13_out, not_3_out, Opcode[1], not_5_out);
  and and_14 (and_14_out, Opcode[3], not_3_out, Opcode[0]);
  and and_15 (and_15_out, not_1_out, not_2_out, not_5_out, Funct[1]);
  and and_16 (and_16_out, not_2_out, Opcode[1], not_5_out);
  or or_1 (ALUOpcode[4], and_1_out, and_2_out, and_3_out, and_4_out);
  or or_2 (ALUOpcode[3], and_5_out, and_6_out, and_7_out, and_8_out, and_9_out);
  or or_3 (ALUOpcode[2], and_10_out, and_11_out);
  or or_4 (ALUOpcode[1], and_12_out, and_13_out, and_14_out);
  or or_5 (ALUOpcode[0], and_15_out, and_16_out);
  or or_6 (RegDst[1], decoder_1_out8, decoder_1_out9, decoder_1_out10, decoder_1_out11, MEMRd, RtR7R1[0], RtR7R1[1]);
  or or_7 (ALUSrc, decoder_1_out8, decoder_1_out9, decoder_1_out10, decoder_1_out11, MEMRd, MEMWr);
  or or_8 (EXTOp, MEMRd, MEMWr, decoder_1_out8, isBEQ, isBNE);
  nor nor_1 (RegWR, MEMWr, isBEQ, isBNE, decoder_1_out16);
  or or_9 (WB[1], RtR7R1[0], RtR7R1[1]);
  or or_10 (WB[0], MEMRd, RtR7R1[1]);
  or or_11 (isHump, decoder_1_out16, RtR7R1[0]);
  and and_17 (isJR, RegDst[0], Funct[1], Funct[0]);
endmodule

module pipelinedCtrlEX (
  input  ALUSrc,
  input  [4:0] ALUOp,
  input  isBEQ,
  input  isBNE,
  input  MemWr,
  input  [1:0] WB,
  input  RegWr,
  input  clr,
  output ALUSrcOut,
  output [4:0] ALUOpOut,
  output isBEQOut,
  output isBNEOut,
  output MemWrOut,
  output [1:0] WBOut,
  output RegWrOut
);

  wire clk_out, multiplexer_1_out, multiplexer_3_out, multiplexer_4_out, multiplexer_5_out,
       multiplexer_7_out, undriven;
  wire [1:0] multiplexer_6_out;
  wire [4:0] multiplexer_2_out;

  Clock clk (.out(clk_out));
  Multiplexer multiplexer_1 (.in0(ALUSrc), .in1(1'b0), .out(multiplexer_1_out), .sel(clr));
  Multiplexer #(.width(5)) multiplexer_2 (.in0(ALUOp), .in1({5{1'b0}}), .out(multiplexer_2_out), .sel(clr));
  Multiplexer multiplexer_3 (.in0(isBEQ), .in1(1'b0), .out(multiplexer_3_out), .sel(clr));
  Multiplexer multiplexer_4 (.in0(isBNE), .in1(1'b0), .out(multiplexer_4_out), .sel(clr));
  Multiplexer multiplexer_5 (.in0(MemWr), .in1(1'b0), .out(multiplexer_5_out), .sel(clr));
  Multiplexer #(.width(2)) multiplexer_6 (.in0(WB), .in1(2'b00), .out(multiplexer_6_out), .sel(clr));
  Multiplexer multiplexer_7 (.in0(RegWr), .in1(1'b0), .out(multiplexer_7_out), .sel(clr));
  Register #(.width(1)) register_1 (.D(multiplexer_1_out), .en(1'b1), .Q(ALUSrcOut), .clk(clk_out));  // open: clr
  Register #(.width(5)) register_2 (.D(multiplexer_2_out), .en(1'b1), .Q(ALUOpOut), .clk(clk_out));  // open: clr
  Register #(.width(1)) register_3 (.D(multiplexer_3_out), .en(1'b1), .Q(isBEQOut), .clk(clk_out));  // open: clr
  Register #(.width(1)) register_4 (.D(multiplexer_4_out), .en(1'b1), .Q(isBNEOut), .clk(clk_out));  // open: clr
  Register #(.width(1)) register_5 (.D(multiplexer_5_out), .en(1'b1), .Q(MemWrOut), .clk(clk_out));  // open: clr
  Register #(.width(2)) register_6 (.D(multiplexer_6_out), .en(1'b1), .Q(WBOut), .clk(clk_out), .clr(undriven));
  Register #(.width(1)) register_7 (.D(multiplexer_7_out), .en(1'b1), .Q(RegWrOut), .clk(clk_out));  // open: clr
endmodule

module pipelinedCtrMEM (
  input  MemWr,
  input  [1:0] WB,
  input  RegWr,
  output MemWrOut,
  output [1:0] WBOut,
  output RegWrOut
);

  wire clk_out;

  Clock clk (.out(clk_out));
  Register #(.width(1)) register_1 (.D(MemWr), .en(1'b1), .Q(MemWrOut), .clk(clk_out), .clr(1'b0));
  Register #(.width(2)) register_2 (.D(WB), .en(1'b1), .Q(WBOut), .clk(clk_out), .clr(1'b0));
  Register #(.width(1)) register_3 (.D(RegWr), .en(1'b1), .Q(RegWrOut), .clk(clk_out), .clr(1'b0));
endmodule

module pipelinedPC (
  input  isBEQ,
  input  isBNE,
  input  isJump,
  input  isJr,
  input  zero,
  output [1:0] PCOp,
  output kill1,
  output kill2
);

  wire and_1_out, and_2_out, and_3_out, and_4_out, and_5_out, decoder_1_out0, decoder_1_out2, decoder_1_out3,
       not_1_out, not_2_out, not_3_out, not_4_out, not_5_out, not_6_out, not_7_out;

  not not_1 (not_1_out, isJr);
  not not_2 (not_2_out, zero);
  not not_3 (not_3_out, isBNE);
  not not_4 (not_4_out, isJump);
  not not_5 (not_5_out, isBEQ);
  and and_1 (and_1_out, isBEQ, zero);
  and and_2 (and_2_out, isBNE, not_2_out);
  and and_3 (and_3_out, not_7_out, not_6_out, isJr);
  not not_6 (not_6_out, and_1_out);
  not not_7 (not_7_out, and_2_out);
  and and_4 (and_4_out, isJump, not_6_out, not_7_out);
  and and_5 (and_5_out, not_6_out, not_7_out, isJr);
  or or_1 (PCOp[0], and_1_out, and_2_out, and_3_out);
  or or_2 (PCOp[1], and_4_out, and_5_out);
  Decoder #(.enable("false"), .select(2)) decoder_1 (
    .out0(decoder_1_out0), .out1(kill2), .out2(decoder_1_out2), .out3(decoder_1_out3), .sel(PCOp));
  or or_3 (kill1, kill2, decoder_1_out2, decoder_1_out3);
endmodule

module dataHazDet (
  input  MemRd2,
  input  [2:0] Rd2,
  input  [2:0] RsOpcode,
  input  [2:0] RtOpcode,
  input  RegWrite2,
  input  [2:0] Rd3,
  input  RegWrite3,
  input  [2:0] Rd4,
  input  RegWrite4,
  output [1:0] frwrdA,
  output [1:0] frwrdB,
  output stall
);

  wire and_1_out, and_2_out, and_3_out, and_4_out, and_5_out, and_6_out, and_7_out, and_8_out, and_9_out,
       and_10_out, and_11_out, and_12_out, and_13_out, and_14_out, areopsame_1_areequal,
       areopsame_2_areequal, areopsame_3_areequal, areopsame_4_areequal, areopsame_5_areequal,
       areopsame_6_areequal, not_1_out, not_2_out, not_3_out, not_4_out, not_5_out, not_6_out;

  areOpSame areopsame_1 (.reg1(Rd2), .reg2(RsOpcode), .areEqual(areopsame_1_areequal));
  areOpSame areopsame_2 (.reg1(Rd2), .reg2(RtOpcode), .areEqual(areopsame_2_areequal));
  areOpSame areopsame_3 (.reg1(Rd3), .reg2(RsOpcode), .areEqual(areopsame_3_areequal));
  areOpSame areopsame_4 (.reg1(Rd3), .reg2(RtOpcode), .areEqual(areopsame_4_areequal));
  areOpSame areopsame_5 (.reg1(Rd4), .reg2(RsOpcode), .areEqual(areopsame_5_areequal));
  areOpSame areopsame_6 (.reg1(Rd4), .reg2(RtOpcode), .areEqual(areopsame_6_areequal));
  and and_1 (and_1_out, areopsame_3_areequal, RegWrite3);
  and and_2 (and_2_out, areopsame_4_areequal, RegWrite3);
  and and_3 (and_3_out, areopsame_5_areequal, RegWrite4);
  and and_4 (and_4_out, areopsame_6_areequal, RegWrite4);
  and and_5 (and_5_out, areopsame_1_areequal, RegWrite2);
  and and_6 (and_6_out, areopsame_2_areequal, RegWrite2);
  not not_1 (not_1_out, and_4_out);
  not not_2 (not_2_out, and_3_out);
  not not_3 (not_3_out, and_1_out);
  not not_4 (not_4_out, and_2_out);
  not not_5 (not_5_out, and_6_out);
  not not_6 (not_6_out, and_5_out);
  and and_7 (and_7_out, not_6_out, not_3_out, and_3_out);
  and and_8 (and_8_out, not_6_out, and_1_out);
  and and_9 (and_9_out, not_6_out, not_3_out, and_3_out);
  and and_10 (and_10_out, not_5_out, not_4_out, and_4_out);
  and and_11 (and_11_out, not_5_out, and_2_out);
  and and_12 (and_12_out, not_5_out, not_4_out, and_4_out);
  and and_13 (and_13_out, MemRd2, and_5_out);
  and and_14 (and_14_out, MemRd2, and_6_out);
  or or_1 (frwrdA[0], and_5_out, and_7_out);
  or or_2 (frwrdA[1], and_8_out, and_9_out);
  or or_3 (frwrdB[0], and_6_out, and_10_out);
  or or_4 (frwrdB[1], and_11_out, and_12_out);
  or or_5 (stall, and_13_out, and_14_out);
endmodule

module areOpSame (
  input  [2:0] reg1,
  input  [2:0] reg2,
  output areEqual
);

  Comparator #(.mode("unsigned"), .width(3)) comparator_1 (.a(reg1), .b(reg2), .eq(areEqual));  // open: gt, lt
endmodule

module isLUI (
  input  [4:0] Opcode2,
  output isLUI
);

  and and_1 (isLUI, Opcode2[0], Opcode2[1], Opcode2[2], Opcode2[3], Opcode2[4]);
endmodule

module oldPPPC (
  input  in_1,
  input  in_2,
  input  in_3,
  input  in_4,
  input  in_5
);

  wire and_1_out, and_2_out, and_3_out, and_4_out, not_1_out, not_2_out, not_3_out, not_4_out, not_5_out;
  wire [1:0] or_1_out;

  not not_1 (not_1_out, in_5);
  not not_2 (not_2_out, in_4);
  not not_3 (not_3_out, in_2);
  not not_4 (not_4_out, in_3);
  not not_5 (not_5_out, in_1);
  and and_1 (and_1_out, in_1, in_5);
  and and_2 (and_2_out, in_2, not_1_out);
  and and_3 (and_3_out, not_5_out, not_3_out, in_4);
  and and_4 (and_4_out, not_5_out, not_3_out, in_3);
  or or_1 (or_1_out[0], and_1_out, and_2_out, and_3_out);
  or or_2 (or_1_out[1], and_4_out, in_4);
endmodule
